// Logisim project project 3.circ as structural Verilog: 2 circuits, main circuit solution
module solution (
  input  [3:0] A,
  input  [3:0] B,
  output [3:0] Q,
  output R
);

  wire one_bit_adder_1_c_out, one_bit_adder_2_c_out, one_bit_adder_3_c_out;

  // Probe on A
  // Probe on B
  one_bit_adder one_bit_adder_1 (.A(A[0]), .B(B[0]), .C_in(1'b0), .SUM(R), .C_out(one_bit_adder_1_c_out));
  one_bit_adder one_bit_adder_2 (
    .A(A[1]), .B(B[1]), .C_in(one_bit_adder_1_c_out), .SUM(Q[0]), .C_out(one_bit_adder_2_c_out));
  one_bit_adder one_bit_adder_3 (
    .A(A[2]), .B(B[2]), .C_in(one_bit_adder_2_c_out), .SUM(Q[1]), .C_out(one_bit_adder_3_c_out));
  one_bit_adder one_bit_adder_4 (.A(A[3]), .B(B[3]), .C_in(one_bit_adder_3_c_out), .SUM(Q[2]), .C_out(Q[3]));
  // Probe on Q
endmodule

module one_bit_adder (
  input  A,
  input  B,
  input  C_in,
  output SUM,
  output C_out
);

  wire and_1_out, and_2_out, and_3_out;

  and and_1 (and_1_out, A, B);
  and and_2 (and_2_out, C_in, B);
  and and_3 (and_3_out, A, C_in);
  xor xor_1 (SUM, A, B, C_in);
  or or_1 (C_out, and_1_out, and_2_out, and_3_out);
endmodule
